# Fritzing sketch Relays_power_supply (saved by Fritzing 0.9.3b)
breadboards: 1

parts:
  Part1 = Arduino Mega 2560 (Rev3)
  WeMos_D1_Mini_Relay_Shield_V1 = WeMos D1 Mini Relay Shield V2
  WeMos_D1_Mini_Relay_Shield_V2 = WeMos D1 Mini Relay Shield V2
  WeMos_D1_Mini_Relay_Shield_V3 = WeMos D1 Mini Relay Shield V2
  VCC1 = Battery block 9V
  U1 = Voltage Regulator [package=to-220-alt]

nets:
  GND: Part1.GND, WeMos_D1_Mini_Relay_Shield_V1.G, WeMos_D1_Mini_Relay_Shield_V2.G, WeMos_D1_Mini_Relay_Shield_V3.G, VCC1.-, U1.GND
  N1: Part1.D22, WeMos_D1_Mini_Relay_Shield_V1.D1
  N2: Part1.D23, WeMos_D1_Mini_Relay_Shield_V2.D1
  N3: Part1.D24, WeMos_D1_Mini_Relay_Shield_V3.D1
  5V: WeMos_D1_Mini_Relay_Shield_V1.5V, WeMos_D1_Mini_Relay_Shield_V2.5V, WeMos_D1_Mini_Relay_Shield_V3.5V, U1.OUT
  N4: VCC1.+, U1.IN
