# Fritzing sketch BT_separate_power (saved by Fritzing 0.9.3b)
breadboards: 1

parts:
  Part1 = Arduino Mega 2560 (Rev3)
  Part3 = Bluetooth Mate Silver
  VCC1 = Battery
  VCC2 = Battery

nets:
  N1: Part1.D19/RX1, Part3.TX_5V
  N2: Part1.D18/TX1, Part3.RX_5V
  GND: Part1.GND, Part3.GND, VCC2.-
  N3: Part3.VCC, VCC1.+
  N4: VCC1.-, VCC2.+
