# Fritzing sketch BT_separate_power_9V (saved by Fritzing 0.9.3b)
breadboards: 1

parts:
  Part1 = Arduino Mega 2560 (Rev3)
  Part3 = Bluetooth Mate Silver
  U1 = Voltage Regulator - 5V [package="TO220 [THT]"]
  VCC1 = Battery block 9V

nets:
  N1: Part1.D19/RX1, Part3.TX_5V
  N2: Part1.D18/TX1, Part3.RX_5V
  GND: Part1.GND, Part3.GND, U1.input_voltage, VCC1.-
  N3: Part3.VCC, U1.output_voltage
  N4: U1.GND, VCC1.+
