# Fritzing sketch bt_led_mic (saved by Fritzing 0.9.3b)
breadboards: 1

parts:
  Part1 = Arduino Mega 2560 (Rev3)
  Part2 = Bluetooth Mate Silver
  Part3 = Breakout Board for Electret Microphone
  LED1 = LED - 5mm [color="Red (633nm)" package="5 mm [THT]"]
  R1 = Resistor [tolerance=±5% resistance=1k package=THT]
  LED2 = LED - 5mm [color="Red (633nm)" package="5 mm [THT]"]

nets:
  N1: Part1.A0, Part3.AUD
  N2: Part1.D19/RX1, Part2.TX_5V
  N3: Part1.D18/TX1, Part2.RX_5V
  GND: Part1.GND, Part2.GND, Part3.GND, LED1.cathode, LED2.cathode
  N4: Part1.D13_PWM, LED2.anode
  3V3: Part1.3V3, Part3.VCC
  5V: Part1.5V, Part2.VCC
  N5: Part1.D7_PWM, R1.Pin_1
  N6: LED1.anode, R1.Pin_0
