# Fritzing sketch circuit_3_relays_not_working (saved by Fritzing 0.9.3b)
breadboards: 2

parts:
  Part1 = Arduino Mega 2560 (Rev3)
  IC1 = Voltage Regulator [package=78xxl]
  WeMos_D1_Mini_Relay_Shield_V2 = WeMos D1 Mini Relay Shield V2
  WeMos_D1_Mini_Relay_Shield_V3 = WeMos D1 Mini Relay Shield V2
  WeMos_D1_Mini_Relay_Shield_V1 = WeMos D1 Mini Relay Shield V2
  Part2 = Adafruit MPR121
  C1 = Electrolytic Capacitor [capacitance=10µF package="100 mil [THT, electrolytic]"]

nets:
  N1: Part1.D21/SCL, Part2.SCL
  N2: Part1.D20/SDA, Part2.SDA
  GND: Part1.GND, IC1.GND, WeMos_D1_Mini_Relay_Shield_V2.G, WeMos_D1_Mini_Relay_Shield_V3.G, WeMos_D1_Mini_Relay_Shield_V1.G, Part2.GND, C1.-
  N3: Part1.VIN, IC1.IN
  5V: Part1.5V, Part2.VIN, C1.+
  N4: Part1.D22, WeMos_D1_Mini_Relay_Shield_V1.D1
  N5: Part1.D23, WeMos_D1_Mini_Relay_Shield_V2.D1
  N6: Part1.D24, WeMos_D1_Mini_Relay_Shield_V3.D1
  5V_2: IC1.OUT, WeMos_D1_Mini_Relay_Shield_V2.5V, WeMos_D1_Mini_Relay_Shield_V3.5V, WeMos_D1_Mini_Relay_Shield_V1.5V

notes:
  to relays
  from 9V wall adapter
  relay 1
  relay 2
  relay 3
  10 uF

custom parts:
  Adafruit MPR121: Add lots of touch sensors to your next microcontroller project with this easy-to-use 12-channel capacitive touch sensor breakout board, starring the MPR121. This chip can handle up to 12 individual touch pads. The MPR121 has support for only I2C, which can be implemented with nearly any microcontroller. You can select one of 4 addresses with the ADDR pin, for a total of 48 capacitive touch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
