# Fritzing sketch relay_power_supply (saved by Fritzing 0.9.3b)
breadboards: 1

parts:
  Part1 = Arduino Mega 2560 (Rev3)
  IC1 = Voltage Regulator [package=78xxl]

nets:
  GND: Part1.GND, IC1.GND
  N1: Part1.VIN, IC1.IN

notes:
  to relays
  from 9V wall adapter
