# Fritzing sketch relay_power_supply_2 (saved by Fritzing 0.9.3b)
breadboards: 1

parts:
  Part1 = Arduino Mega 2560 (Rev3)
  IC1 = Voltage Regulator [package=78xxl]
  JACK1 = 2.1mm Barrel Jack with Terminal Block

nets:
  GND: Part1.GND, IC1.GND, JACK1.NEG
  N1: IC1.IN, JACK1.POS

notes:
  to relays
  from 9V wall adapter
