# Fritzing sketch station_7_def_circuit (saved by Fritzing 0.9.3b)
breadboards: 2

parts:
  Part1 = Bare Conductive Touch Board
  Part2 = Lithium Ion Polymer Battery 3.7v 2000mAh [part_number=2011]  # not connected
  J1 = Basic Servo
  J2 = Basic Servo
  VCC1 = Battery
  VCC2 = Battery
  U1 = 2.5mm Audio Jack [package=stereojack2.5mm_specia_pogopins]

nets:
  GND: Part1.GND, J1.gnd, J2.gnd, VCC2.-
  N1: Part1.L, U1.LEFT
  N2: Part1.R, U1.RIGHT
  N3: Part1.AGND, U1.SLEEVE
  VCC: J1.vcc, J2.vcc, VCC1.+
  N4: VCC1.-, VCC2.+

custom parts:
  Lithium Ion Polymer Battery 3.7v 2000mAh: Lithium ion polymer (also known as 'lipo' or 'lipoly') batteries are thin, light and powerful. The output ranges from 4.2V when completely charged to 3.7V. This battery has a capacity of 2000mAh. The batteries come pre-attached with a genuine 2-pin JST-PH connector as shown and include the necessary protection circuitry.
