# Fritzing sketch more_servos (saved by Fritzing 0.9.3b)
breadboards: 2

parts:
  VCC1 = Battery block 9V
  J1 = Basic Servo
  J2 = Basic Servo
  VCC3 = Battery
  VCC2 = Battery
  Part1 = Arduino Uno (Rev3)

nets:
  GND: VCC1.-, J1.gnd, J2.gnd, VCC3.-, Part1.GND
  N1: VCC1.+, Part1.VIN
  VCC: J1.vcc, J2.vcc, VCC2.+
  N2: J1.pulse, Part1.D6_PWM
  N3: J2.pulse, Part1.D5_PWM
  N4: VCC3.+, VCC2.-
